// Digital circuit mul_by_n.dig as structural Verilog
module mul_by_n (
  input  [3:0] in,
  output [7:0] out
);

  wire [3:0] add_1_s;
  wire [4:4] add_1_c_o;

  Add #(.Bits(4)) add_1 (.a(in), .b(in), .c_i(1'b0), .s(add_1_s), .c_o(add_1_c_o[4]));
  Add #(.Bits(5)) add_2 (.a({1'b0, in}), .b({add_1_c_o[4], add_1_s}), .c_i(1'b0), .s(out[4:0]), .c_o(out[5]));

  assign out[7:6] = 2'b00;
endmodule
