// Digital circuit abs-submit.dig as structural Verilog
module abs_submit (
  input  [3:0] in,
  output sign,
  output [3:0] out
);

  wire [2:0] xor_1_out;

  xor xor_1 (xor_1_out[2], in[3], in[2]);
  xor xor_2 (xor_1_out[1], in[3], in[1]);
  xor xor_3 (xor_1_out[0], in[3], in[0]);
  Add #(.Bits(3)) add_1 (.a({2'b00, in[3]}), .b(xor_1_out), .c_i(1'b0), .s(out[2:0]), .c_o(out[3]));

  assign sign = in[3];
endmodule
