// Digital circuit sevensegment.dig as structural Verilog
module sevensegment (
  input  in_1,
  input  in_2,
  input  in_3
);

  wire oct2seven_1_a, oct2seven_1_b, oct2seven_1_c, oct2seven_1_d, oct2seven_1_e, oct2seven_1_f,
       oct2seven_1_g;

  oct2seven oct2seven_1 (
    .d2(in_1), .d1(in_2), .d0(in_3), .a(oct2seven_1_a), .b(oct2seven_1_b), .c(oct2seven_1_c),
    .d(oct2seven_1_d), .e(oct2seven_1_e), .f(oct2seven_1_f), .g(oct2seven_1_g));
  Seven_Seg seven_seg_1 (
    .a(oct2seven_1_a), .b(oct2seven_1_b), .c(oct2seven_1_c), .d(oct2seven_1_d), .e(oct2seven_1_e),
    .f(oct2seven_1_f), .g(oct2seven_1_g), .dp(1'b0));
endmodule
