// Digital circuit template.dig as structural Verilog
module template (
  input  MSB__A,
  input  B,
  input  LSB__C
);

  wire not_1_out, not_2_out, not_3_out, xor_1_out, xor_2_out;

  not not_1 (not_1_out, MSB__A);
  not not_2 (not_2_out, B);
  not not_3 (not_3_out, LSB__C);
  LED led_1 (.in(MSB__A));
  LED led_2 (.in(B));
  LED led_3 (.in(LSB__C));
  xor xor_1 (xor_1_out, MSB__A, B);
  xor xor_2 (xor_2_out, B, LSB__C);
  LED led_4 (.in(MSB__A));
  LED led_5 (.in(xor_1_out));
  LED led_6 (.in(xor_2_out));

  // Notes on the sheet:
  //   A
  //   B
  //   C
  //   INPUT
  //   X
  //   Y
  //   Z
  //   OUTPUT
endmodule
