// Digital circuit tally.dig as structural Verilog
module tally (
  input  clk,
  input  reset,
  input  button,
  output [3:0] t10,
  output [3:0] t1
);

  wire and_1_out, and_2_out, and_3_out, and_4_out, and_5_out, cntdecu_2_p5, d_ff_1_nq, d_ff_1_q, d_ff_2_nq,
       d_ff_2_q, d_ff_3_q, not_1_out, not_2_out, or_1_out, or_2_out, xor_1_out, xor_2_out;

  not not_1 (not_1_out, reset);
  not not_2 (not_2_out, button);
  xor xor_1 (xor_1_out, d_ff_2_q, d_ff_1_q);
  and and_1 (and_1_out, d_ff_2_nq, d_ff_1_nq, not_2_out);
  D_FF d_ff_1 (.D(and_1_out), .C(clk), .Q(d_ff_1_q), .nQ(d_ff_1_nq));
  and and_2 (and_2_out, not_2_out, xor_1_out);
  D_FF d_ff_2 (.D(and_2_out), .C(clk), .Q(d_ff_2_q), .nQ(d_ff_2_nq));
  and and_3 (and_3_out, cntdecu_2_p5, and_5_out, d_ff_1_q);
  xor xor_2 (xor_2_out, d_ff_3_q, or_2_out);
  and and_4 (and_4_out, d_ff_1_q, cntdecu_2_p5);
  D_FF d_ff_3 (.D(xor_2_out), .C(clk), .Q(d_ff_3_q));  // open: nQ
  or or_1 (or_1_out, and_3_out, not_1_out);
  or or_2 (or_2_out, and_4_out, not_1_out);
  and and_5 (and_5_out, d_ff_3_q, d_ff_1_q);
  // cntDECu cntdecu_1: pin names not known; wires that end beside it: clk, or_1_out, or_2_out, t10
  // cntDECu cntdecu_2: pin names not known; wires that end beside it: clk, or_2_out, d_ff_1_q, t1, cntdecu_2_p5
endmodule
