// Digital circuit 4bitadder.dig as structural Verilog
module _4bitadder (
  input  [3:0] A,
  input  [3:0] B,
  input  Cin,
  output Cout,
  output [3:0] SUM
);

  wire fulladder_1_cout, fulladder_2_cout, fulladder_3_cout;

  fulladder fulladder_1 (.A(A[0]), .B(B[0]), .Cin(Cin), .Cout(fulladder_1_cout), .SUM(SUM[0]));
  fulladder fulladder_2 (.A(A[1]), .B(B[1]), .Cin(fulladder_1_cout), .Cout(fulladder_2_cout), .SUM(SUM[1]));
  fulladder fulladder_3 (.A(A[2]), .B(B[2]), .Cin(fulladder_2_cout), .Cout(fulladder_3_cout), .SUM(SUM[2]));
  fulladder fulladder_4 (.A(A[3]), .B(B[3]), .Cin(fulladder_3_cout), .Cout(Cout), .SUM(SUM[3]));
endmodule
