// Digital circuit BCDadder.dig as structural Verilog
module BCDadder (
  input  [3:0] A,
  input  [3:0] B,
  input  Cin,
  output Cout,
  output [3:0] SUM
);

  wire _4bitadder_1_cout, and_1_out, and_2_out;
  wire [2:2] or_1_out;
  wire [3:0] _4bitadder_1_sum;

  _4bitadder _4bitadder_1 (.A(A), .B(B), .Cin(Cin), .Cout(_4bitadder_1_cout), .SUM(_4bitadder_1_sum));
  and and_1 (and_1_out, _4bitadder_1_sum[2], _4bitadder_1_sum[3]);
  and and_2 (and_2_out, _4bitadder_1_sum[1], _4bitadder_1_sum[3]);
  or or_1 (or_1_out[2], and_1_out, and_2_out, _4bitadder_1_cout);
  _4bitadder _4bitadder_2 (
    .A(_4bitadder_1_sum), .B({1'b0, {2{or_1_out[2]}}, 1'b0}), .Cin(1'b0), .Cout(Cout), .SUM(SUM));
endmodule
