// Digital circuit calculator.dig as structural Verilog
module calculator (
  input  [3:0] DATA,
  input  DA,
  input  CLK,
  output [3:0] D0,
  output [3:0] D1,
  output [3:0] D2,
  output [3:0] D3,
  output [3:0] D4,
  output [3:0] D5,
  output [3:0] D6,
  output [3:0] D7
);

  wire bcdadder_1_cout, bcdadder_2_cout, bcdadder_3_cout, bcdadder_4_cout, bcdadder_5_cout, bcdadder_6_cout,
       bcdadder_7_cout;
  wire [1:0] controller_1_mux1, controller_1_mux2;
  wire [3:0] bcdadder_1_sum, bcdadder_2_sum, bcdadder_3_sum, bcdadder_4_sum, bcdadder_5_sum, bcdadder_6_sum,
       bcdadder_7_sum, bcdadder_8_sum, multiplexer_1_out, multiplexer_2_out, multiplexer_3_out,
       multiplexer_4_out, multiplexer_5_out, multiplexer_6_out, multiplexer_7_out, multiplexer_8_out,
       multiplexer_9_out, multiplexer_10_out, multiplexer_11_out, multiplexer_12_out, multiplexer_13_out,
       multiplexer_14_out, multiplexer_15_out, multiplexer_16_out, register4bit_2_q_3_0,
       register4bit_4_q_3_0, register4bit_6_q_3_0, register4bit_8_q_3_0, register4bit_10_q_3_0,
       register4bit_12_q_3_0, register4bit_14_q_3_0, register4bit_16_q_3_0;

  controller controller_1 (.DATA(DATA), .DA(DA), .CLK(CLK), .MUX1(controller_1_mux1), .MUX2(controller_1_mux2));
  Multiplexer #(.Selector_Bits(2), .Bits(4)) multiplexer_1 (
    .sel(controller_1_mux1), .in_0(D0), .in_1(4'b0000), .in_2(bcdadder_1_sum), .in_3(DATA),
    .out(multiplexer_1_out));
  Multiplexer #(.Selector_Bits(2), .Bits(4)) multiplexer_2 (
    .sel(controller_1_mux2), .in_0(register4bit_2_q_3_0), .in_1(4'b0000), .in_2(bcdadder_1_sum),
    .in_3(register4bit_2_q_3_0), .out(multiplexer_2_out));
  register4bit register4bit_1 (.D_3_0(multiplexer_1_out), .CLK(CLK), .Q_3_0(D0));
  register4bit register4bit_2 (.D_3_0(multiplexer_2_out), .CLK(CLK), .Q_3_0(register4bit_2_q_3_0));
  BCDadder bcdadder_1 (.A(D0), .B(register4bit_2_q_3_0), .Cin(1'b0), .Cout(bcdadder_1_cout), .SUM(bcdadder_1_sum));
  Multiplexer #(.Selector_Bits(2), .Bits(4)) multiplexer_3 (
    .sel(controller_1_mux1), .in_0(D1), .in_1(4'b0000), .in_2(bcdadder_2_sum), .in_3(D0),
    .out(multiplexer_3_out));
  Multiplexer #(.Selector_Bits(2), .Bits(4)) multiplexer_4 (
    .sel(controller_1_mux2), .in_0(register4bit_4_q_3_0), .in_1(4'b0000), .in_2(bcdadder_2_sum),
    .in_3(register4bit_4_q_3_0), .out(multiplexer_4_out));
  register4bit register4bit_3 (.D_3_0(multiplexer_3_out), .CLK(CLK), .Q_3_0(D1));
  register4bit register4bit_4 (.D_3_0(multiplexer_4_out), .CLK(CLK), .Q_3_0(register4bit_4_q_3_0));
  BCDadder bcdadder_2 (
    .A(D1), .B(register4bit_4_q_3_0), .Cin(bcdadder_1_cout), .Cout(bcdadder_2_cout), .SUM(bcdadder_2_sum));
  Multiplexer #(.Selector_Bits(2), .Bits(4)) multiplexer_5 (
    .sel(controller_1_mux1), .in_0(D2), .in_1(4'b0000), .in_2(bcdadder_3_sum), .in_3(D1),
    .out(multiplexer_5_out));
  Multiplexer #(.Selector_Bits(2), .Bits(4)) multiplexer_6 (
    .sel(controller_1_mux2), .in_0(register4bit_6_q_3_0), .in_1(4'b0000), .in_2(bcdadder_3_sum),
    .in_3(register4bit_6_q_3_0), .out(multiplexer_6_out));
  register4bit register4bit_5 (.D_3_0(multiplexer_5_out), .CLK(CLK), .Q_3_0(D2));
  register4bit register4bit_6 (.D_3_0(multiplexer_6_out), .CLK(CLK), .Q_3_0(register4bit_6_q_3_0));
  BCDadder bcdadder_3 (
    .A(D2), .B(register4bit_6_q_3_0), .Cin(bcdadder_2_cout), .Cout(bcdadder_3_cout), .SUM(bcdadder_3_sum));
  Multiplexer #(.Selector_Bits(2), .Bits(4)) multiplexer_7 (
    .sel(controller_1_mux1), .in_0(D3), .in_1(4'b0000), .in_2(bcdadder_4_sum), .in_3(D2),
    .out(multiplexer_7_out));
  Multiplexer #(.Selector_Bits(2), .Bits(4)) multiplexer_8 (
    .sel(controller_1_mux2), .in_0(register4bit_8_q_3_0), .in_1(4'b0000), .in_2(bcdadder_4_sum),
    .in_3(register4bit_8_q_3_0), .out(multiplexer_8_out));
  register4bit register4bit_7 (.D_3_0(multiplexer_7_out), .CLK(CLK), .Q_3_0(D3));
  register4bit register4bit_8 (.D_3_0(multiplexer_8_out), .CLK(CLK), .Q_3_0(register4bit_8_q_3_0));
  BCDadder bcdadder_4 (
    .A(D3), .B(register4bit_8_q_3_0), .Cin(bcdadder_3_cout), .Cout(bcdadder_4_cout), .SUM(bcdadder_4_sum));
  Multiplexer #(.Selector_Bits(2), .Bits(4)) multiplexer_9 (
    .sel(controller_1_mux1), .in_0(D4), .in_1(4'b0000), .in_2(bcdadder_5_sum), .in_3(D3),
    .out(multiplexer_9_out));
  Multiplexer #(.Selector_Bits(2), .Bits(4)) multiplexer_10 (
    .sel(controller_1_mux2), .in_0(register4bit_10_q_3_0), .in_1(4'b0000), .in_2(bcdadder_5_sum),
    .in_3(register4bit_10_q_3_0), .out(multiplexer_10_out));
  register4bit register4bit_9 (.D_3_0(multiplexer_9_out), .CLK(CLK), .Q_3_0(D4));
  register4bit register4bit_10 (.D_3_0(multiplexer_10_out), .CLK(CLK), .Q_3_0(register4bit_10_q_3_0));
  BCDadder bcdadder_5 (
    .A(D4), .B(register4bit_10_q_3_0), .Cin(bcdadder_4_cout), .Cout(bcdadder_5_cout), .SUM(bcdadder_5_sum));
  Multiplexer #(.Selector_Bits(2), .Bits(4)) multiplexer_11 (
    .sel(controller_1_mux1), .in_0(D5), .in_1(4'b0000), .in_2(bcdadder_6_sum), .in_3(D4),
    .out(multiplexer_11_out));
  Multiplexer #(.Selector_Bits(2), .Bits(4)) multiplexer_12 (
    .sel(controller_1_mux2), .in_0(register4bit_12_q_3_0), .in_1(4'b0000), .in_2(bcdadder_6_sum),
    .in_3(register4bit_12_q_3_0), .out(multiplexer_12_out));
  register4bit register4bit_11 (.D_3_0(multiplexer_11_out), .CLK(CLK), .Q_3_0(D5));
  register4bit register4bit_12 (.D_3_0(multiplexer_12_out), .CLK(CLK), .Q_3_0(register4bit_12_q_3_0));
  BCDadder bcdadder_6 (
    .A(D5), .B(register4bit_12_q_3_0), .Cin(bcdadder_5_cout), .Cout(bcdadder_6_cout), .SUM(bcdadder_6_sum));
  Multiplexer #(.Selector_Bits(2), .Bits(4)) multiplexer_13 (
    .sel(controller_1_mux1), .in_0(D6), .in_1(4'b0000), .in_2(bcdadder_7_sum), .in_3(D5),
    .out(multiplexer_13_out));
  Multiplexer #(.Selector_Bits(2), .Bits(4)) multiplexer_14 (
    .sel(controller_1_mux2), .in_0(register4bit_14_q_3_0), .in_1(4'b0000), .in_2(bcdadder_7_sum),
    .in_3(register4bit_14_q_3_0), .out(multiplexer_14_out));
  register4bit register4bit_13 (.D_3_0(multiplexer_13_out), .CLK(CLK), .Q_3_0(D6));
  register4bit register4bit_14 (.D_3_0(multiplexer_14_out), .CLK(CLK), .Q_3_0(register4bit_14_q_3_0));
  BCDadder bcdadder_7 (
    .A(D6), .B(register4bit_14_q_3_0), .Cin(bcdadder_6_cout), .Cout(bcdadder_7_cout), .SUM(bcdadder_7_sum));
  Multiplexer #(.Selector_Bits(2), .Bits(4)) multiplexer_15 (
    .sel(controller_1_mux1), .in_0(D7), .in_1(4'b0000), .in_2(bcdadder_8_sum), .in_3(D6),
    .out(multiplexer_15_out));
  Multiplexer #(.Selector_Bits(2), .Bits(4)) multiplexer_16 (
    .sel(controller_1_mux2), .in_0(register4bit_16_q_3_0), .in_1(4'b0000), .in_2(bcdadder_8_sum),
    .in_3(register4bit_16_q_3_0), .out(multiplexer_16_out));
  register4bit register4bit_15 (.D_3_0(multiplexer_15_out), .CLK(CLK), .Q_3_0(D7));
  register4bit register4bit_16 (.D_3_0(multiplexer_16_out), .CLK(CLK), .Q_3_0(register4bit_16_q_3_0));
  BCDadder bcdadder_8 (.A(D7), .B(register4bit_16_q_3_0), .Cin(bcdadder_7_cout), .SUM(bcdadder_8_sum));  // open: Cout
endmodule
