// Digital circuit controller.dig as structural Verilog
module controller (
  input  [3:0] DATA,
  input  DA,
  input  CLK,
  output [1:0] MUX1,
  output [1:0] MUX2
);

  wire A_2_nq, A_2_q, A_nq, A_q, and_1_out, and_2_out, and_3_out, and_4_out, and_5_out, and_6_out, and_7_out,
       B_2_nq, B_2_q, B_nq, B_q, or_1_out, or_2_out, reset_1_rst, xor_1_out;
  wire [3:0] d_ff_1_q, multiplexer_1_out;

  and and_1 (and_1_out, A_q, DA);
  and and_2 (and_2_out, A_nq, DA, B_nq);
  or or_1 (or_1_out, and_1_out, B_q);
  D_FF A (.D(or_1_out), .C(CLK), .Q(A_q), .nQ(A_nq));
  D_FF B (.D(and_2_out), .C(CLK), .Q(B_q), .nQ(B_nq));
  and and_3 (and_3_out, B_q, and_4_out);
  Multiplexer #(.Bits(4)) multiplexer_1 (.sel(and_5_out), .in_0(d_ff_1_q), .in_1(DATA), .out(multiplexer_1_out));
  and and_4 (and_4_out, B_2_nq, A_2_nq);
  D_FF #(.Bits(4)) d_ff_1 (.D(multiplexer_1_out), .C(CLK), .Q(d_ff_1_q));  // open: nQ
  or or_2 (or_2_out, A_2_q, and_3_out);
  and and_5 (and_5_out, B_2_q, A_2_nq);
  xor xor_1 (xor_1_out, A_2_q, B_2_q);
  and and_6 (and_6_out, or_2_out, B_2_nq);
  and and_7 (and_7_out, d_ff_1_q[3], d_ff_1_q[2], d_ff_1_q[1]);
  D_FF A_2 (.D(xor_1_out), .C(CLK), .Q(A_2_q), .nQ(A_2_nq));
  D_FF B_2 (.D(and_6_out), .C(CLK), .Q(B_2_q), .nQ(B_2_nq));
  mux1 mux1_1 (.A(A_2_q), .B(B_2_q), .R(reset_1_rst), .P1(and_7_out), .P2(d_ff_1_q[0]), .MX1(MUX1));
  mux2 mux2_1 (.A(A_2_q), .B(B_2_q), .P1(and_7_out), .P2(d_ff_1_q[0]), .MX2(MUX2));
  reset reset_1 (.A(A_2_q), .B(B_2_q), .P1(and_7_out), .P2(d_ff_1_q[0]), .CLK(CLK), .RST(reset_1_rst));  // open: RSTP

  // Notes on the sheet:
  //   Start detection
  //   Load data into FF if state==01
  //   To deassert start when state
  //   is no longer 0
  //   Main-ASM
  //   P1
  //   P2
endmodule
