// Digital circuit fulladder.dig as structural Verilog
module fulladder (
  input  A,
  input  B,
  input  Cin,
  output Cout,
  output SUM
);

  wire and_1_out, and_2_out, xor_1_out;

  and and_1 (and_1_out, A, B);
  xor xor_1 (xor_1_out, A, B);
  xor xor_2 (SUM, xor_1_out, Cin);
  and and_2 (and_2_out, xor_1_out, Cin);
  or or_1 (Cout, and_1_out, and_2_out);
endmodule
