// Digital circuit mux1.dig as structural Verilog
module mux1 (
  input  A,
  input  B,
  input  R,
  input  P1,
  input  P2,
  output [1:0] MX1
);

  wire and_1_out, and_2_out, and_3_out, and_4_out, and_5_out, not_1_out, not_2_out, not_3_out, not_4_out,
       not_5_out, not_6_out;

  not not_1 (not_1_out, A);
  not not_2 (not_2_out, B);
  not not_3 (not_3_out, P2);
  not not_4 (not_4_out, B);
  not not_5 (not_5_out, P1);
  not not_6 (not_6_out, P1);
  and and_1 (and_1_out, A, not_4_out, not_5_out);
  and and_2 (and_2_out, A, not_4_out, P2);
  and and_3 (and_3_out, not_1_out, B, R);
  and and_4 (and_4_out, A, not_2_out, P1, not_3_out);
  and and_5 (and_5_out, A, not_2_out, not_6_out);
  or or_1 (MX1[1], and_1_out, and_2_out);
  or or_2 (MX1[0], and_3_out, and_4_out, and_5_out);
endmodule
