// Digital circuit mux2.dig as structural Verilog
module mux2 (
  input  A,
  input  B,
  input  P1,
  input  P2,
  output [1:0] MX2
);

  wire and_1_out, and_2_out, and_3_out, not_1_out, not_2_out, not_3_out;

  not not_1 (not_1_out, B);
  not not_2 (not_2_out, P1);
  not not_3 (not_3_out, P2);
  and and_1 (and_1_out, A, not_1_out, not_2_out);
  and and_2 (and_2_out, A, not_1_out, not_3_out);
  and and_3 (and_3_out, A, not_1_out, P2);
  or or_1 (MX2[0], and_1_out, and_2_out);
  or or_2 (MX2[1], and_1_out, and_3_out);
endmodule
