// Digital circuit register4bit.dig as structural Verilog
module register4bit (
  input  [3:0] D_3_0,
  input  CLK,
  output [3:0] Q_3_0
);

  D_FF d_ff_1 (.D(D_3_0[0]), .C(CLK), .Q(Q_3_0[0]));  // open: nQ
  D_FF d_ff_2 (.D(D_3_0[1]), .C(CLK), .Q(Q_3_0[1]));  // open: nQ
  D_FF d_ff_3 (.D(D_3_0[2]), .C(CLK), .Q(Q_3_0[2]));  // open: nQ
  D_FF d_ff_4 (.D(D_3_0[3]), .C(CLK), .Q(Q_3_0[3]));  // open: nQ
endmodule
