// Digital circuit reset.dig as structural Verilog
module reset (
  input  A,
  input  B,
  input  P1,
  input  P2,
  input  CLK,
  output RST,
  output RSTP
);

  wire and_1_out, and_2_out, and_3_out, and_4_out, and_5_out, not_1_out, not_2_out, not_3_out, or_1_out;

  not not_1 (not_1_out, B);
  not not_2 (not_2_out, P1);
  not not_3 (not_3_out, A);
  and and_1 (and_1_out, RST, A, P1);
  and and_2 (and_2_out, RST, A, B);
  and and_3 (and_3_out, A, not_1_out, P1, P2);
  and and_4 (and_4_out, not_1_out, not_2_out, RST);
  and and_5 (and_5_out, not_1_out, not_3_out, RST);
  or or_1 (or_1_out, and_1_out, and_2_out, and_3_out, and_4_out, and_5_out);
  D_FF RESET (.D(or_1_out), .C(CLK), .Q(RST), .nQ(RSTP));
endmodule
