// Digital circuit encoder.dig as structural Verilog
module encoder (
  input  _0,
  input  _1,
  input  _2,
  input  _3,
  input  _4,
  input  _5,
  input  _6,
  input  _7,
  input  _8,
  input  _9,
  input  A,
  input  B,
  input  C,
  input  D,
  input  E,
  input  F,
  input  CLK,
  output [3:0] DATA,
  output DA
);

  wire priorityencoder_1_any;
  wire [3:0] multiplexer_1_out, priorityencoder_1_num;

  PriorityEncoder #(.Selector_Bits(4)) priorityencoder_1 (
    .in0(_0), .in1(_1), .in2(_2), .in3(_3), .in4(_4), .in5(_5), .in6(_6), .in7(_7), .in8(_8), .in9(_9),
    .in10(A), .in11(B), .in12(C), .in13(D), .in14(E), .in15(F), .num(priorityencoder_1_num),
    .any(priorityencoder_1_any));
  Multiplexer #(.Bits(4)) multiplexer_1 (
    .sel(priorityencoder_1_any), .in_0(DATA), .in_1(priorityencoder_1_num), .out(multiplexer_1_out));
  D_FF #(.Bits(4)) d_ff_1 (.D(multiplexer_1_out), .C(CLK), .Q(DATA));  // open: nQ
  D_FF d_ff_2 (.D(priorityencoder_1_any), .C(CLK), .Q(DA));  // open: nQ
endmodule
