// Digital circuit project.dig as structural Verilog
module project (
  input  clk
);

  wire _0_out, _1_out, _2_out, _3_out, _4_out, _5_out, _6_out, _7_out, _8_out, _9_out, A_out, B_out, C_out,
       D_out, E_out, encoder_1_da, F_out;
  wire [3:0] calculator_1_d0, calculator_1_d1, calculator_1_d2, calculator_1_d3, calculator_1_d4,
       calculator_1_d5, calculator_1_d6, calculator_1_d7, encoder_1_data;

  Button _0 (.out(_0_out));
  Button _4 (.out(_4_out));
  Button _8 (.out(_8_out));
  Button C (.out(C_out));
  Button _1 (.out(_1_out));
  Button _5 (.out(_5_out));
  Button _9 (.out(_9_out));
  Button D (.out(D_out));
  Button _2 (.out(_2_out));
  Button _6 (.out(_6_out));
  Button A (.out(A_out));
  Button E (.out(E_out));
  Button _3 (.out(_3_out));
  Button _7 (.out(_7_out));
  Button B (.out(B_out));
  Button F (.out(F_out));
  encoder encoder_1 (
    ._0(_0_out), ._1(_1_out), ._2(_2_out), ._3(_3_out), ._4(_4_out), ._5(_5_out), ._6(_6_out), ._7(_7_out),
    ._8(_8_out), ._9(_9_out), .A(A_out), .B(B_out), .C(C_out), .D(D_out), .E(E_out), .F(F_out), .CLK(clk),
    .DATA(encoder_1_data), .DA(encoder_1_da));
  calculator calculator_1 (
    .DATA(encoder_1_data), .DA(encoder_1_da), .CLK(clk), .D0(calculator_1_d0), .D1(calculator_1_d1),
    .D2(calculator_1_d2), .D3(calculator_1_d3), .D4(calculator_1_d4), .D5(calculator_1_d5),
    .D6(calculator_1_d6), .D7(calculator_1_d7));
  Seven_Seg_Hex seven_seg_hex_1 (.d(calculator_1_d7), .dp(1'b0));
  Seven_Seg_Hex seven_seg_hex_2 (.d(calculator_1_d6), .dp(1'b0));
  Seven_Seg_Hex seven_seg_hex_3 (.d(calculator_1_d5), .dp(1'b0));
  Seven_Seg_Hex seven_seg_hex_4 (.d(calculator_1_d4), .dp(1'b0));
  Seven_Seg_Hex seven_seg_hex_5 (.d(calculator_1_d3), .dp(1'b0));
  Seven_Seg_Hex seven_seg_hex_6 (.d(calculator_1_d2), .dp(1'b0));
  Seven_Seg_Hex seven_seg_hex_7 (.d(calculator_1_d1), .dp(1'b0));
  Seven_Seg_Hex seven_seg_hex_8 (.d(calculator_1_d0), .dp(1'b0));

  // Notes on the sheet:
  //   clk: Hz: 100
endmodule
